# Fritzing sketch Useless-Machine-Schematic (saved by Fritzing 0.9.2b)
breadboards: 1

parts:
  MOSFET_(Optional) = Basic FET P-Channel [package="TO220 [THT]"]
  part = Resistor [tolerance=±5% resistance=10k package=THT]
  C1 = Electrolytic Capacitor [capacitance=100µF package="100 mil [THT, electrolytic]"]
  ON/OFF_Switch = Toggle Switch [package=THT]
  CoverServo = Basic Servo
  FingerServo = Basic Servo
  Part2 = Arduino Nano (Rev3.0)
  U1 = Voltage Regulator - 5V [package="TO220 [THT]"]
  +12_v = Power plug

nets:
  N1: MOSFET_(Optional).gate, Part2.D11/MOSI
  GND: MOSFET_(Optional).drain, C1.-, CoverServo.gnd, FingerServo.gnd
  GND_2: MOSFET_(Optional).source, part.Pin_0, Part2.GND, U1.GND, +12_v.GND
  N2: part.Pin_1, ON/OFF_Switch.L2, Part2.D2
  VCC: C1.+, CoverServo.vcc, FingerServo.vcc, U1.output_voltage
  N3: ON/OFF_Switch.COM, Part2.5V
  N4: CoverServo.pulse, Part2.D10
  N5: FingerServo.pulse, Part2.D9
  VIN: Part2.VIN, U1.input_voltage, +12_v.VCC
